// Logisim project MCTE 2332 PROJECT - ZHAO YAQI 1739844.circ as structural Verilog: 1 circuit, main circuit main
module main (
  input  Key_Code_1,
  input  Key_Code_2,
  input  Key_Code_3,
  input  Key_Code_4,
  input  ENTER,
  input  Data_Entry_1,
  input  Data_Entry_2,
  input  Data_Entry_3,
  input  Data_Entry_4
);

  wire nor_1_out, nor_2_out, nor_3_out, or_1_out, or_2_out, or_3_out, xor_1_out, xor_2_out, xor_3_out,
       xor_4_out;

  xor xor_1 (xor_1_out, Key_Code_1, Data_Entry_1);
  xor xor_2 (xor_2_out, Key_Code_2, Data_Entry_2);
  xor xor_3 (xor_3_out, Key_Code_3, Data_Entry_3);
  xor xor_4 (xor_4_out, Key_Code_4, Data_Entry_4);
  or or_1 (or_1_out, xor_1_out, xor_2_out);
  or or_2 (or_2_out, xor_3_out, xor_4_out);
  or or_3 (or_3_out, or_1_out, or_2_out);
  not nor_1 (nor_1_out, or_3_out);  // NOR_Gate
  nor nor_2 (nor_2_out, nor_1_out, ENTER);
  LED NOT_GO (.in(nor_2_out));
  LED GO (.in(nor_3_out));
  nor nor_3 (nor_3_out, or_3_out, ENTER);

  // Notes on the sheet:
  //   A
  //   B
  //   C
  //   D
  //   E
  //   F
  //   G
  //   H
  //   I
  //   J
endmodule
